// Logisim project seq.circ as structural Verilog: 5 circuits, main circuit main
module main (
  input  ALU_Out1,
  input  Maybe1,
  input  nCLK4,
  input  CLK8,
  input  CLK9,
  input  NMI,
  input  CLK6,
  input  w,
  input  CLK4,
  input  SeqControl_2,
  input  CLK1,
  input  CLK2,
  input  SYNC_RESET,
  input  d,
  input  SeqControl_1,
  input  RESET,
  input  x41,
  input  [7:0] IR,
  input  OSC_STABLE,
  input  WAKE,
  output a20,
  output a22,
  output a24,
  output RD,
  output a3,
  output a1
);

  wire and_1_out, and_2_out, and_3_out, and_4_out, and_5_out, and_6_out, and_7_out, g18_out, g19_out,
       g20_out, g21_out, g22_out, g23_out, g24_out, g25_out, g28_out, g29_out, g32_out, g33_q, g34_out,
       g35_q, g36_q, g37_q, g40_out, g41_out, g50_out, g51_out, g53_out, g54_q, g55_nq, g56_out, g68_q,
       g69_out, g70_out, g71_q, g86_out, g87_out, g88_out, g89_q, g90_out, g92_q, g93_out, g94_q, g95_out,
       multiplexer_1_out, multiplexer_2_out, nand_1_out, nor_1_out, nor_2_out, nor_3_out, nor_4_out,
       nor_5_out, not_1_out, or_1_out, undriven, undriven_2, undriven_3, undriven_4, undriven_5, undriven_6,
       undriven_7, undriven_8, undriven_9, undriven_10, undriven_11, undriven_12, undriven_13, undriven_14,
       undriven_15, undriven_16, undriven_17, undriven_18;

  not g53 (g53_out, NMI);
  dff g54 (.ck(CLK8), .cck(CLK9), .d(g53_out), .q(g54_q));
  nor g50 (g50_out, undriven, SYNC_RESET, 1'b0);
  not g51 (g51_out, g50_out);
  latch g55 (.clk(CLK8), .cclk(CLK9), .d(g54_q), .nq(g55_nq));
  not g41 (g41_out, undriven_2);
  and and_1 (and_1_out, g41_out, undriven_4, CLK4);
  and and_2 (and_2_out, undriven_5, undriven_3);
  nor g87 (g87_out, SYNC_RESET, x41);
  nor g56 (g56_out, g55_nq, g53_out);
  nor nor_1 (nor_1_out, and_1_out, g51_out);
  nor nor_2 (nor_2_out, and_2_out, SYNC_RESET);
  not g86 (g86_out, g68_q);
  not g88 (g88_out, g87_out);
  not g40 (g40_out, nor_1_out);
  rs g71 (.nr(nor_2_out), .s(g56_out), .q(g71_q));
  rs g89 (.nr(g86_out), .s(g88_out), .q(g89_q));
  nand g70 (g70_out, g40_out, g94_q, g71_q);
  not g69 (g69_out, g70_out);
  dff g94 (.ck(CLK8), .cck(CLK9), .d(g89_q), .q(g94_q));
  and and_3 (and_3_out, g94_q, x41);
  and and_4 (and_4_out, undriven_6, undriven_7);
  not g95 (g95_out, undriven_7);
  rs g68 (.nr(nor_2_out), .s(g69_out), .q(g68_q));
  nor nor_3 (nor_3_out, and_3_out, and_4_out);
  Multiplexer multiplexer_1 (.in0(1'b1), .in1(nor_3_out), .out(multiplexer_1_out), .sel(CLK4));
  and and_5 (and_5_out, undriven_8, g94_q);
  nor nor_4 (nor_4_out, and_5_out, and_6_out, SYNC_RESET);
  and and_6 (and_6_out, undriven_6, g95_out);
  not not_1 (not_1_out, SYNC_RESET);
  Multiplexer multiplexer_2 (.in0(not_1_out), .in1(nor_4_out), .out(multiplexer_2_out), .sel(CLK4));
  not g93 (g93_out, multiplexer_1_out);
  rs g92 (.nr(multiplexer_2_out), .s(g93_out), .q(g92_q));
  nand g90 (g90_out, g92_q, g89_q);
  not g18 (g18_out, undriven_9);
  not g20 (g20_out, undriven_10);
  not g22 (g22_out, undriven_11);
  nor g24 (g24_out, ALU_Out1, g51_out);
  not g32 (g32_out, CLK6);
  not g34 (g34_out, undriven_12);
  nand g19 (g19_out, g18_out, g24_out);
  nand g21 (g21_out, g20_out, g24_out);
  nand g23 (g23_out, g22_out, g24_out);
  nor g25 (g25_out, Maybe1, nCLK4);
  latchr g33 (
    .clk(CLK6), .cclk(g32_out), .ld(undriven_12), .nld(g34_out), .d(undriven_13), .res(undriven_14), .q(g33_q));
  not g29 (g29_out, undriven_17);
  or or_1 (or_1_out, undriven_15, undriven_16);
  and and_7 (and_7_out, g29_out, g33_q);
  nor g28 (g28_out, undriven_18, g51_out, 1'b0);
  dff g35 (.ck(CLK8), .cck(CLK9), .d(g19_out), .q(g35_q));
  dff g36 (.ck(CLK8), .cck(CLK9), .d(g21_out), .q(g36_q));
  dff g37 (.ck(CLK8), .cck(CLK9), .d(g23_out), .q(g37_q));
  nand nand_1 (nand_1_out, or_1_out, g25_out);
  nor nor_5 (nor_5_out, and_7_out, 1'b0);
  not g12 (a20, g35_q);
  not g14 (a22, g36_q);
  not g16 (a24, g37_q);
  not g27 (RD, nand_1_out);
  not g10 (a3, nor_5_out);
  not g1 (a1, g28_out);

  // Notes on the sheet:
  //   1: Bus disable
  //   /NMI
  //   CLK_DIS
  //   s3_op_reti_s011
  //   NMI Edge detect
  //   d102
  //   s1_op_cb_s0xx
  //   w26
  //   s2_m1
  //   clk_dis_or_sync_reset
  //   d93
  //   s1_int_s110
  //   SeqOut_1
  //   g39
  //   g52
  //   d99
  //   s1_op_di_ei_s0xx
  //   Interrupt sequence start
  //   IR[3]
  //   Interrupt sequence end
  //   g94
  //   g91
  //   [!] Non-demorganized circuit
  //   The decoder commands when to switch state.
  //   clk_dis_or_sync_reset
  //   s2_state2_next
  //   s2_state1_next
  //   s2_state0_next
  //   w32
  //   w33
  //   w20
  //   w26
  //   s2_m1
  //   s1_op_cb_s0xx
  //   CLK_DIS
  //   d102
  //   TODO
  //   Sequence state & modes
  //   w26
  //   w18
  //   s2_m1
  //   s2_data_fetch_cycle
  //   g26
  //   g30
  //   #State2
  //   #State1
  //   #State0
  //   cb_mode
  //   intr_dispatch
  //   Extra decoder inputs
  //   Extra decoder inputs
endmodule

module dff (
  input  ck,
  input  cck,
  input  d,
  output q
);
endmodule

module latch (
  input  clk,
  input  cclk,
  input  d,
  output nq
);
endmodule

module rs (
  input  nr,
  input  s,
  output q
);
endmodule

module latchr (
  input  clk,
  input  cclk,
  input  ld,
  input  nld,
  input  d,
  input  res,
  output q
);
endmodule
